# Fritzing sketch finalCircWiringDiagram (saved by Fritzing 0.9.9b)
stripboards: 1

parts:
  Part1 = Arduino Uno (Rev3)
  U1 = WS2812 RGB LED strip
  Part2 = Thumb Joystick
  R1 = Resistor [tolerance=±5% resistance=220 package="0402 [SMD]"]
  C1 = Electrolytic Capacitor [capacitance=1000μF voltage=6.3V package="1010 [SMD, electrolytic]"]
  JACK1 = 2.1mm Barrel Jack with Terminal Block

nets:
  N1: Part1.A0, Part2.HORZ
  N2: Part1.A1, Part2.VERT
  N3: Part1.D2, Part2.SEL
  N4: Part1.D7, R1.Pin_1
  VCC: Part1.5V, U1.VCC, Part2.VCC, C1.+, JACK1.POS
  GND: Part1.GND, U1.GND, Part2.GND, C1.-, JACK1.NEG
  N5: U1.DIN, R1.Pin_0

custom parts:
  WS2812 RGB LED strip: WS2812 strip
